# Fritzing sketch ControlNode_SMG (saved by Fritzing 0.9.3b)
circuit board: 12.0335cm x 6.31681cm
breadboards: 1

parts:
  M1 = DOIT Esp32 DevKit v1 (30 pins long, 11 pins width) [part_number=ESP32S-PIN30]
  Bus_current = ACS712 Low Current Sensor Board v12
  M2 = RioRand LM2596
  Gen_current = ACS712 Low Current Sensor Board v12
  SSR3 = Screw terminal - 2 pins [package=THT]
  SSR2 = Screw terminal - 2 pins [package=THT]
  SSR1 = Screw terminal - 2 pins [package=THT]
  12vin = Screw terminal - 2 pins [package=THT]
  U1 = TRANSISTOR_NPN_2 [package=to-92]
  U2 = TRANSISTOR_NPN_2 [package=to-92]
  U3 = TRANSISTOR_NPN_2 [package=to-92]
  LED1 = LED - 3mm [color="Red (633nm)" package="3 mm [THT]"]
  LED2 = LED - 3mm [color="Red (633nm)" package="3 mm [THT]"]
  LED3 = LED - 3mm [color="Red (633nm)" package="3 mm [THT]"]
  220_1 = Resistor [tolerance=±5% resistance=220 package=THT]
  220_2 = Resistor [tolerance=±5% resistance=220 package=THT]
  220_3 = Resistor [tolerance=±5% resistance=220 package=THT]
  RB1k = Resistor [tolerance=±5% resistance=220 package=THT]
  RB1K_2 = Resistor [tolerance=±5% resistance=220 package=THT]
  RB1K_3 = Resistor [tolerance=±5% resistance=220 package=THT]
  PD10K_1 = Resistor [tolerance=±5% resistance=220 package=THT]
  PD10K_2 = Resistor [tolerance=±5% resistance=220 package=THT]
  PD10K_3 = Resistor [tolerance=±5% resistance=220 package=THT]
  Self_current = ACS712 Low Current Sensor Board v12
  Bus_voltage = Voltage Sensor 25V
  Gen_voltage = Voltage Sensor 25V
  S1 = Pushbutton [package="[THT]"]
  10K = Resistor [tolerance=±5% resistance=220 package=THT]

nets:
  5V: M1.3V3, Bus_current.5V, Gen_current.5V, Self_current.5V, Bus_voltage.+, Gen_voltage.+, S1.Pin_1, S1.Pin_2
  GND: M1.GND, Bus_current.GND, M2.Pin_2, M2.Pin_4, Gen_current.GND, 12vin.pin2, U1.E, U2.E, U3.E, LED1.cathode, LED2.anode, LED3.anode, PD10K_1.Pin_0, PD10K_2.Pin_0, PD10K_3.Pin_0, Self_current.GND, Bus_voltage.GND, Bus_voltage.-, Gen_voltage.GND, Gen_voltage.-, 10K.Pin_1
  N1: M1.D19, S1.Pin_3, S1.Pin_4, 10K.Pin_0
  N2: M1.D21, 220_1.Pin_0
  N3: M1.D22, 220_2.Pin_0
  N4: M1.D23, 220_3.Pin_0
  N5: M1.VP, Bus_voltage.S
  N6: M1.VN, Gen_voltage.S
  N7: M1.D34, Bus_current.VO
  N8: M1.D35, Gen_current.VO
  N9: M1.D32, Self_current.VO
  N10: M1.D25, RB1K_3.Pin_1, PD10K_3.Pin_1
  N11: M1.D26, RB1K_2.Pin_1, PD10K_2.Pin_1
  N12: M1.D27, RB1k.Pin_1, PD10K_1.Pin_1
  N13: M1.VIN, Self_current.IP+
  N14: M2.Pin_1, SSR3.pin1, SSR2.pin1, SSR1.pin1, 12vin.pin1
  N15: M2.Pin_3, Self_current.IP-
  N16: SSR3.pin2, U3.C
  N17: SSR2.pin2, U1.C
  N18: SSR1.pin2, U2.C
  N19: U1.B, RB1K_2.Pin_0
  N20: U2.B, RB1k.Pin_0
  N21: U3.B, RB1K_3.Pin_0
  N22: LED1.anode, 220_1.Pin_1
  N23: LED2.cathode, 220_2.Pin_1
  N24: LED3.cathode, 220_3.Pin_1

custom parts:
  DOIT Esp32 DevKit v1 (30 pins long, 11 pins width): The DOIT Esp32 DevKit v1 is one of the development board created by DOIT to evaluate the ESP-WROOM-32 module. It is based on the ESP32 microcontroller that boasts Wifi, Bluetooth, Ethernet and Low Power support all in a single chip. (vanepp) made breadboard work, adjusted pin numbering and labels and reduced size of schematic and cleaned up pcb. This chip is 30pins long (2 x15) and 11 pins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
